// Logisim project r4other.circ as structural Verilog: 1 circuit, main circuit main
module main (
  input  A,
  input  B,
  output W,
  output X,
  output Y,
  output Z
);

  wire not_1_out, not_2_out, xor_1_out;

  xor xor_1 (xor_1_out, A, B);
  not not_1 (not_1_out, A);
  not not_2 (not_2_out, B);
  not not_3 (W, xor_1_out);
  and and_1 (X, not_1_out, B);
  and and_2 (Y, A, not_2_out);
  and and_3 (Z, A, B);
endmodule
